# Fritzing sketch Ble-1 (saved by Fritzing 0.9.2b)
breadboards: 1

parts:
  Componente1 = Arduino Uno (Rev3)
  R1 = Resistor [tolerance=±5% resistance=220 package=THT]
  IC1 = MakerStudio BLE
  LED1 = LED - 5mm [color="Red (633nm)" package="5 mm [THT]"]

nets:
  N1: Componente1.D10_PWM/SS, IC1.RX
  N2: Componente1.D11_PWM/MOSI, IC1.TX
  N3: Componente1.D4, R1.Pin_1
  5V: Componente1.5V, IC1.5V
  GND: Componente1.GND, IC1.GND, LED1.cathode
  N4: R1.Pin_0, LED1.anode
